// Digital circuit Pipelined MIPS Datapath.dig as structural Verilog
module Pipelined_MIPS_Datapath (
);

  wire alu_1_zero, ALUSrc, and_1_out, Branch, Branch_Add_c_o, CLK, MemRead, MemToReg, MemWrite, not_1_out,
       PC_plus_4_2_nq, PC_plus_4_c_o, RegDst, RegWrite, Zero_nq, Zero_q;
  wire [3:0] ALUOp;
  wire [4:0] multiplexer_2_out, Rd_nq, Rd_q, RegDst_2_q, RegDst_nq, RegDst_q, Rt_nq, Rt_q;
  wire [27:0] Branch_Add_s, Branching_nq, Branching_q, d_ff_1_nq, d_ff_1_q, multiplexer_1_out, PC_plus_4_2_q,
       PC_plus_4_s, PC_q;
  wire [31:0] alu_1_result, ALUResult_nq, ALUResult_q, barrelshifter_1_out, bitextender_1_out, Data_Memory_d,
       Imm_nq, Imm_q, Instruction_Memory_d, Instruction_nq, multiplexer_3_out, multiplexer_4_out, RD2_2_q,
       RD2_nq, RD2_q, ReadData1_nq, ReadData1_q, ReadData2_nq, ReadData2_q, ReadData_q, Register_File_da,
       Register_File_db;
  wire [32:0] Instruction_q;

  Register #(.Bits(28), .isProgramCounter("true")) PC (.D(multiplexer_1_out), .C(CLK), .Q(PC_q));  // open: en
  Multiplexer multiplexer_1 (.sel(and_1_out), .in_0(PC_plus_4_s[0]), .in_1(Branching_q[0]), .out(multiplexer_1_out[0]));
  Add #(.Bits(28)) PC_plus_4 (.a(PC_q), .b(28'h4), .c_i(1'b0), .s(PC_plus_4_s), .c_o(PC_plus_4_c_o));
  ROM #(.AddrBits(24), .isProgramMemory("true"), .Bits(32)) Instruction_Memory (
    .A(PC_q[23:0]), .sel(1'b1), .D(Instruction_Memory_d));
  D_FF #(.Bits(28)) d_ff_1 (.D(PC_plus_4_s), .C(CLK), .Q(d_ff_1_q), .nQ(d_ff_1_nq));
  D_FF #(.Bits(32)) Instruction (.D(Instruction_Memory_d), .C(CLK), .Q(Instruction_q[31:0]), .nQ(Instruction_nq));
  RegisterFile #(.AddrBits(5), .Bits(32)) Register_File (
    .Din(multiplexer_4_out), .we(RegWrite), .Rw(RegDst_2_q), .C(not_1_out), .Ra(Instruction_q[25:21]),
    .Rb(Instruction_q[20:16]), .Da(Register_File_da), .Db(Register_File_db));
  not not_1 (not_1_out, CLK);
  BitExtender #(.inputBits(16), .outputBits(32)) bitextender_1 (.in(Instruction_q[15:0]), .out(bitextender_1_out));
  D_FF PC_plus_4_2 (.D(d_ff_1_q[0]), .C(CLK), .Q(PC_plus_4_2_q[0]), .nQ(PC_plus_4_2_nq));
  D_FF #(.Bits(32)) ReadData1 (.D(Register_File_da), .C(CLK), .Q(ReadData1_q), .nQ(ReadData1_nq));
  D_FF #(.Bits(32)) ReadData2 (.D(Register_File_db), .C(CLK), .Q(ReadData2_q), .nQ(ReadData2_nq));
  D_FF #(.Bits(32)) Imm (.D(bitextender_1_out), .C(CLK), .Q(Imm_q), .nQ(Imm_nq));
  D_FF #(.Bits(5)) Rt (.D(Instruction_q[20:16]), .C(CLK), .Q(Rt_q), .nQ(Rt_nq));
  D_FF #(.Bits(5)) Rd (.D(Instruction_q[15:11]), .C(CLK), .Q(Rd_q), .nQ(Rd_nq));
  Multiplexer #(.Bits(5)) multiplexer_2 (.sel(RegDst), .in_0(Rt_q), .in_1(Rd_q), .out(multiplexer_2_out));
  BarrelShifter #(.Bits(32)) barrelshifter_1 (.in(Imm_q), .shift(2'b10), .out(barrelshifter_1_out));
  Multiplexer #(.Bits(32)) multiplexer_3 (.sel(ALUSrc), .in_0(ReadData2_q), .in_1(Imm_q), .out(multiplexer_3_out));
  Add #(.Bits(28)) Branch_Add (
    .a(PC_plus_4_2_q), .b(barrelshifter_1_out[27:0]), .c_i(1'b0), .s(Branch_Add_s), .c_o(Branch_Add_c_o));
  ALU alu_1 (.Op1(ReadData1_q), .Op2(multiplexer_3_out), .Opcode(ALUOp), .Zero(alu_1_zero), .Result(alu_1_result));
  D_FF #(.Bits(28)) Branching (.D(Branch_Add_s), .C(CLK), .Q(Branching_q), .nQ(Branching_nq));
  D_FF Zero (.D(alu_1_zero), .C(CLK), .Q(Zero_q), .nQ(Zero_nq));
  D_FF #(.Bits(32)) ALUResult (.D(alu_1_result), .C(CLK), .Q(ALUResult_q), .nQ(ALUResult_nq));
  D_FF #(.Bits(32)) RD2 (.D(ReadData2_q), .C(CLK), .Q(RD2_q), .nQ(RD2_nq));
  D_FF #(.Bits(5)) u_RegDst (.D(multiplexer_2_out), .C(CLK), .Q(RegDst_q), .nQ(RegDst_nq));
  and and_1 (and_1_out, Branch, Zero_q);
  RAMDualPort #(.AddrBits(24), .Bits(32)) Data_Memory (
    .A(ALUResult_q[23:0]), .Din(RD2_q), .str(MemWrite), .C(CLK), .ld(MemRead), .D(Data_Memory_d));
  D_FF #(.Bits(32)) ReadData (.D(Data_Memory_d), .Q(ReadData_q));  // open: C, nQ
  D_FF #(.Bits(32)) RD2_2 (.D(RD2_q), .Q(RD2_2_q));  // open: C, nQ
  D_FF #(.Bits(5)) RegDst_2 (.D(RegDst_q), .Q(RegDst_2_q));  // open: C, nQ
  Multiplexer multiplexer_4 (.sel(MemToReg), .in_0(RD2_2_q[0]), .in_1(ReadData_q[0]), .out(multiplexer_4_out[0]));
  // Pins of 1 and 28 bits meet at multiplexer_1_out
  // Pins of 24 and 28 bits meet at PC_q
  // Pins of 1 and 28 bits meet at PC_plus_4_s
  // Pins of 1 and 32 bits meet at multiplexer_4_out
  // Pins of 1 and 28 bits meet at Branching_q
  // Pins of 32 and 33 bits meet at Instruction_q
  // Pins of 1 and 32 bits meet at Instruction_nq
  // Pins of 1 and 28 bits meet at d_ff_1_q
  // Pins of 1 and 28 bits meet at d_ff_1_nq
  // Pins of 1 and 32 bits meet at ReadData1_nq
  // Pins of 1 and 32 bits meet at ReadData2_nq
  // Pins of 1 and 5 bits meet at Rt_nq
  // also tied to GND on the sheet: {PC_plus_4_c_o, d_ff_1_nq[0], Instruction_nq[0], PC_plus_4_2_nq, ReadData1_nq[0], ReadData2_nq[0], Imm_nq[0], Rt_nq[0], Rd_nq[0], Branch_Add_c_o, Branching_nq[0], Zero_nq, ALUResult_nq[0], RD2_nq[0], RegDst_nq[0]}
endmodule
